# Fritzing sketch dancing_light_schematic (saved by Fritzing 1.0.5)
breadboards: 1

parts:
  LED1 = LED - 5mm [color="Red (633nm)" current=0.030A package="5 mm [THT]"]  # not connected
  LED2 = LED - 5mm [color="Red (633nm)" current=0.030A package="5 mm [THT]"]
  LED3 = LED - 5mm [color="Red (633nm)" current=0.030A package="5 mm [THT]"]
  LED4 = LED - 5mm [color="Red (633nm)" current=0.030A package="5 mm [THT]"]
  R1 = Resistor [tolerance=±5% power=0.25W resistance=220 package=THT]
  R2 = Resistor [tolerance=±5% power=0.25W resistance=220 package=THT]
  R3 = Resistor [tolerance=±5% power=0.25W resistance=220 package=THT]
  R4 = Resistor [tolerance=±5% power=0.25W resistance=220 package=THT]
  Part1 = Arduino Uno (Rev3)
  LED5 = LED - 5mm [color="Red (633nm)" current=0.030A package="5 mm [THT]"]
  S1 = Pushbutton [package="[THT]"]
  S2 = Pushbutton [package="[THT]"]
  S3 = Pushbutton [package="[THT]"]
  R5 = Resistor [tolerance=±5% power=0.25W resistance=220 package=THT]
  R6 = Resistor [tolerance=±5% power=0.25W resistance=220 package=THT]
  R7 = Resistor [tolerance=±5% power=0.25W resistance=220 package=THT]

nets:
  N1: LED2.cathode, R2.Pin_0
  N2: LED2.anode, Part1.D4
  N3: LED3.cathode, R4.Pin_0
  N4: LED3.anode, Part1.D3_PWM
  N5: LED4.cathode, R3.Pin_0
  N6: LED4.anode, Part1.D2
  N7: R1.Pin_0, LED5.cathode
  N8: R1.Pin_1, R2.Pin_1, R3.Pin_1, R4.Pin_1, Part1.GND, S1.Pin_1, S1.Pin_2, S2.Pin_1, S2.Pin_2, S3.Pin_3, S3.Pin_4, R5.Pin_0, R6.Pin_0, R7.Pin_0
  N9: Part1.A0, S1.Pin_3
  N10: Part1.A1, S2.Pin_3, S2.Pin_4
  N11: Part1.A2, S3.Pin_1
  N12: Part1.D5_PWM, LED5.anode
  N13: Part1.5V, R5.Pin_1, R6.Pin_1, R7.Pin_1
