# Fritzing sketch potentiometer2_schematic (saved by Fritzing 1.0.5)
breadboards: 1

parts:
  Part1 = Arduino Uno (Rev3)
  R1 = Rotary Potentiometer (Small) [maximum_resistance=10kΩ knob_status=50% power=0.5W package=THT]

nets:
  N1: Part1.A0, R1.wiper
  N2: Part1.5V, R1.leg2
  N3: Part1.GND, R1.leg1
