# Fritzing sketch ultrasonic_schematic (saved by Fritzing 1.0.5)
breadboards: 1

parts:
  Part1 = Arduino Uno (Rev3)
  HC-SR04_Sensor_1 = HC-SR04 Ultrasonic Distance Sensor
  LED1 = LED - 5mm [color="Red (633nm)" current=0.030A package="5 mm [THT]"]

nets:
  N1: Part1.D11_PWM/MOSI, HC-SR04_Sensor_1.TRIG
  N2: Part1.D12/MISO, HC-SR04_Sensor_1.ECHO
  GND: Part1.GND, HC-SR04_Sensor_1.GND, LED1.cathode
  N3: Part1.D3_PWM, LED1.anode
  5V: Part1.5V, HC-SR04_Sensor_1.VCC
