# Fritzing sketch 7_segment (saved by Fritzing 1.0.5)
breadboards: 1

parts:
  Part1 = Arduino Uno (Rev3)
  7_Segment1 = 7 Segment Display
  R1 = Resistor [tolerance=±5% power=0.25W resistance=220 package=THT]
  R2 = Resistor [tolerance=±5% power=0.25W resistance=220 package=THT]
  R3 = Resistor [tolerance=±5% power=0.25W resistance=220 package=THT]
  R4 = Resistor [tolerance=±5% power=0.25W resistance=220 package=THT]
  R5 = Resistor [tolerance=±5% power=0.25W resistance=220 package=THT]
  R6 = Resistor [tolerance=±5% power=0.25W resistance=220 package=THT]
  R7 = Resistor [tolerance=±5% power=0.25W resistance=220 package=THT]

nets:
  N1: Part1.GND, 7_Segment1.common_anode
  N2: Part1.D1/TX, R7.Pin_0
  N3: Part1.D2, R6.Pin_0
  N4: Part1.D3_PWM, R5.Pin_1
  N5: Part1.D4, R4.Pin_1
  N6: Part1.D5_PWM, R3.Pin_1
  N7: Part1.D6_PWM, R2.Pin_0
  N8: Part1.D7, R1.Pin_1
  N9: 7_Segment1.Segment_G, R1.Pin_0
  N10: 7_Segment1.Segment_F, R2.Pin_1
  N11: 7_Segment1.Segment_E, R3.Pin_0
  N12: 7_Segment1.Segment_D, R4.Pin_0
  N13: 7_Segment1.Segment_C, R5.Pin_0
  N14: 7_Segment1.Segment_B, R6.Pin_1
  N15: 7_Segment1.Segment_A, R7.Pin_1
