# Fritzing sketch photocell (saved by Fritzing 1.0.5)
breadboards: 1

parts:
  R1 = Photocell (LDR) [power=0.25W dark_resistance_@0.01lx=300kΩ light_resistance_@100lx=400Ω luminance=10lx package=THT]
  LED1 = LED - 5mm [color="Red (633nm)" current=0.030A package="5 mm [THT]"]
  Part1 = Arduino Uno (Rev3)
  R2 = Resistor [tolerance=±5% power=0.25W resistance=220 package=THT]

nets:
  N1: R1.pin_0, Part1.5V
  N2: R1.pin_1, Part1.A0, R2.Pin_0
  N3: LED1.cathode, Part1.GND, R2.Pin_1
  N4: LED1.anode, Part1.D9_PWM
