# Fritzing sketch speaker (saved by Fritzing 1.0.5)
breadboards: 1

parts:
  J1 = Piezo Speaker
  Part1 = Arduino Uno (Rev3)
  S1 = Pushbutton [package="[THT]"]

nets:
  N1: J1.pin1, Part1.D5_PWM
  N2: J1.pin2, Part1.GND, S1.Pin_3, S1.Pin_4
  N3: Part1.5V, S1.Pin_1, S1.Pin_2
